// Digital circuit Prueba1.dig as structural Verilog
module Prueba1 (
  input  X,
  input  Y,
  input  S,
  output FXYS
);

  wire SNOT, SX, SY;

  _7408 \and  (
    .pin1(X), .pin2(SNOT), .pin3(SX), .pin4(S), .pin5(Y), .pin6(SY), .pin7(1'b0), .pin9(1'b0), .pin10(1'b0),
    .pin12(1'b0), .pin13(1'b0), .pin14(1'b1));  // open: pin8, pin11
  _7432 _7432_1 (
    .pin1(SX), .pin2(SY), .pin3(FXYS), .pin4(1'b0), .pin5(1'b0), .pin7(1'b0), .pin9(1'b0), .pin10(1'b0),
    .pin12(1'b0), .pin13(1'b0), .pin14(1'b1));  // open: pin6, pin8, pin11
  _7404 _7404_1 (
    .pin1(S), .pin2(SNOT), .pin3(1'b0), .pin5(1'b0), .pin7(1'b0), .pin9(1'b0), .pin11(1'b0), .pin13(1'b0),
    .pin14(1'b1));  // open: pin4, pin6, pin8, pin10, pin12
endmodule

/* Test case tesy:
X Y S FXYS
0 0 0 0
0 0 1 0
0 1 0 0
0 1 1 1
1 0 0 1
1 0 1 0
1 1 0 1
1 1 1 1
*/
